# Fritzing sketch Project 1 WackAMole (saved by Fritzing 0.9.4)
breadboards: 1

parts:
  R1 = Resistor [tolerance=±5% resistance=560 package=THT]
  R2 = Resistor [tolerance=±5% resistance=560 package=THT]
  R3 = Resistor [tolerance=±5% resistance=560 package=THT]
  R4 = Resistor [tolerance=±5% resistance=560 package=THT]
  R5 = Resistor [tolerance=±5% resistance=560 package=THT]
  R6 = Resistor [tolerance=±5% resistance=560 package=THT]
  LED1 = LED - 5mm [color="Red (633nm)" package="5 mm [THT]"]
  LED2 = LED - 5mm [color="Green (570nm)" package="5 mm [THT]"]
  LED3 = LED - 5mm [color="Red (633nm)" package="5 mm [THT]"]
  LED4 = LED - 5mm [color="Red (633nm)" package="5 mm [THT]"]
  LED5 = LED - 5mm [color="Red (633nm)" package="5 mm [THT]"]
  LED6 = LED - 5mm [color="Red (633nm)" package="5 mm [THT]"]
  Part1 = Arduino Uno (Rev3)
  Part2 = Thumb Joystick
  S2 = Pushbutton [package="[THT]"]

nets:
  N1: R1.Pin_0, Part1.D12/MISO
  N2: R1.Pin_1, LED1.anode
  N3: R2.Pin_0, Part1.D11_PWM/MOSI
  N4: R2.Pin_1, LED2.anode
  N5: R3.Pin_0, Part1.D10_PWM/SS
  N6: R3.Pin_1, LED3.anode
  N7: R4.Pin_0, Part1.D9_PWM
  N8: R4.Pin_1, LED4.anode
  N9: R5.Pin_0, Part1.D8
  N10: R5.Pin_1, LED5.anode
  N11: R6.Pin_0, Part1.D7
  N12: R6.Pin_1, LED6.anode
  GND: LED1.cathode, LED2.cathode, LED3.cathode, LED4.cathode, LED5.cathode, LED6.cathode, Part1.GND, Part2.GND, S2.Pin_1, S2.Pin_2
  N13: Part1.A3, Part2.HORZ
  N14: Part1.A4/SDA, Part2.VERT
  N15: Part1.D2, S2.Pin_3, S2.Pin_4
  5V: Part1.5V, Part2.VCC
